// Logisim project 07 à 04.circ as structural Verilog: 1 circuit, main circuit main
module main (
  input  in_1,
  output out_2,
  output out_3,
  output out_4
);

  wire and_1_out, j_k_ff_1_qn, j_k_ff_2_qn, j_k_ff_3_qn;

  J_K_Flip_Flop #(.trigger("falling")) j_k_ff_1 (
    .J(1'b1), .clk(in_1), .K(1'b1), .Q(out_2), .Qn(j_k_ff_1_qn), .preset(and_1_out));  // open: reset
  J_K_Flip_Flop #(.trigger("falling")) j_k_ff_2 (
    .J(1'b1), .clk(j_k_ff_1_qn), .K(1'b1), .Q(out_3), .Qn(j_k_ff_2_qn), .preset(and_1_out));  // open: reset
  J_K_Flip_Flop #(.trigger("falling")) j_k_ff_3 (
    .J(1'b1), .clk(j_k_ff_2_qn), .K(1'b1), .Q(out_4), .Qn(j_k_ff_3_qn), .preset(and_1_out));  // open: reset
  and and_1 (and_1_out, j_k_ff_3_qn, out_3, out_2);
endmodule
