// Logisim project Contadores 18-11-2020.circ as structural Verilog: 7 circuits, main circuit main
module main (
);

  wire c0_11_2_out_3, clock_1_out, clock_2_out;
  wire [3:0] c0_5_1_out_2, c0_11_1_out_2, c0_11_2_out_2;

  C0_11 c0_11_1 (.in_1(c0_11_2_out_3), .out_2(c0_11_1_out_2));  // open: out_3
  Hex_Digit_Display hex_digit_display_1 (.value(c0_11_1_out_2));  // open: dp
  Clock clock_1 (.out(clock_1_out));
  Hex_Digit_Display hex_digit_display_2 (.value(c0_11_2_out_2));  // open: dp
  C0_11 c0_11_2 (.in_1(clock_1_out), .out_3(c0_11_2_out_3), .out_2(c0_11_2_out_2));
  Clock clock_2 (.out(clock_2_out));
  C0_5 c0_5_1 (.in_1(clock_2_out), .out_2(c0_5_1_out_2));
  Hex_Digit_Display hex_digit_display_3 (.value(c0_5_1_out_2));  // open: dp
endmodule

module C0_7 (
  input  in_1,
  output [3:0] out_2
);

  J_K_Flip_Flop #(.trigger("falling")) j_k_ff_1 (
    .J(1'b1), .clk(in_1), .K(1'b1), .Q(out_2[0]));  // open: Qn, preset, reset
  J_K_Flip_Flop #(.trigger("falling")) j_k_ff_2 (
    .J(1'b1), .clk(out_2[0]), .K(1'b1), .Q(out_2[1]));  // open: Qn, preset, reset
  J_K_Flip_Flop #(.trigger("falling")) j_k_ff_3 (
    .J(1'b1), .clk(out_2[1]), .K(1'b1), .Q(out_2[2]));  // open: Qn, preset, reset

  assign out_2[3] = 1'b0;
endmodule

module C0_15 (
  input  in_1,
  output [3:0] out_2
);

  J_K_Flip_Flop #(.trigger("falling")) j_k_ff_1 (
    .J(1'b1), .clk(in_1), .K(1'b1), .Q(out_2[0]));  // open: Qn, preset, reset
  J_K_Flip_Flop #(.trigger("falling")) j_k_ff_2 (
    .J(1'b1), .clk(out_2[0]), .K(1'b1), .Q(out_2[1]));  // open: Qn, preset, reset
  J_K_Flip_Flop #(.trigger("falling")) j_k_ff_3 (
    .J(1'b1), .clk(out_2[1]), .K(1'b1), .Q(out_2[2]));  // open: Qn, preset, reset
  J_K_Flip_Flop #(.trigger("falling")) j_k_ff_4 (
    .J(1'b1), .clk(out_2[2]), .K(1'b1), .Q(out_2[3]));  // open: Qn, preset, reset
endmodule

module C0_9 (
  input  in_1,
  output [3:0] out_2
);

  wire and_1_out, j_k_ff_1_qn, j_k_ff_3_qn;

  J_K_Flip_Flop #(.trigger("falling")) j_k_ff_1 (
    .J(1'b1), .clk(in_1), .K(1'b1), .Q(out_2[0]), .Qn(j_k_ff_1_qn), .reset(and_1_out));  // open: preset
  J_K_Flip_Flop #(.trigger("falling")) j_k_ff_2 (
    .J(1'b1), .clk(out_2[0]), .K(1'b1), .Q(out_2[1]), .reset(and_1_out));  // open: Qn, preset
  J_K_Flip_Flop #(.trigger("falling")) j_k_ff_3 (
    .J(1'b1), .clk(out_2[1]), .K(1'b1), .Q(out_2[2]), .Qn(j_k_ff_3_qn), .reset(and_1_out));  // open: preset
  LED led_1 (.in(and_1_out));
  J_K_Flip_Flop #(.trigger("falling")) j_k_ff_4 (
    .J(1'b1), .clk(out_2[2]), .K(1'b1), .Q(out_2[3]), .reset(and_1_out));  // open: Qn, preset
  and and_1 (and_1_out, out_2[3], j_k_ff_3_qn, out_2[1], j_k_ff_1_qn);
endmodule

// C0_9 Seq
module \C0_9_Sequência  (
  input  in_1,
  output [3:0] out_2,
  output out_3
);

  wire and_1_out, j_k_ff_1_qn, j_k_ff_3_qn;

  J_K_Flip_Flop #(.trigger("falling")) j_k_ff_1 (
    .J(1'b1), .clk(in_1), .K(1'b1), .Q(out_2[0]), .Qn(j_k_ff_1_qn), .reset(and_1_out));  // open: preset
  J_K_Flip_Flop #(.trigger("falling")) j_k_ff_2 (
    .J(1'b1), .clk(out_2[0]), .K(1'b1), .Q(out_2[1]), .reset(and_1_out));  // open: Qn, preset
  J_K_Flip_Flop #(.trigger("falling")) j_k_ff_3 (
    .J(1'b1), .clk(out_2[1]), .K(1'b1), .Q(out_2[2]), .Qn(j_k_ff_3_qn), .reset(and_1_out));  // open: preset
  LED led_1 (.in(and_1_out));
  J_K_Flip_Flop #(.trigger("falling")) j_k_ff_4 (
    .J(1'b1), .clk(out_2[2]), .K(1'b1), .Q(out_2[3]), .reset(and_1_out));  // open: Qn, preset
  and and_1 (and_1_out, out_2[3], j_k_ff_3_qn, out_2[1], j_k_ff_1_qn);

  assign out_3 = out_2[3];
endmodule

module C0_5 (
  input  in_1,
  output [3:0] out_2
);

  wire and_1_out, j_k_ff_1_qn, j_k_ff_2_qn;

  J_K_Flip_Flop #(.trigger("falling")) j_k_ff_1 (
    .J(1'b1), .clk(in_1), .K(1'b1), .Q(out_2[0]), .Qn(j_k_ff_1_qn), .reset(and_1_out));  // open: preset
  J_K_Flip_Flop #(.trigger("falling")) j_k_ff_2 (
    .J(1'b1), .clk(out_2[0]), .K(1'b1), .Q(out_2[1]), .Qn(j_k_ff_2_qn), .reset(and_1_out));  // open: preset
  J_K_Flip_Flop #(.trigger("falling")) j_k_ff_3 (
    .J(1'b1), .clk(out_2[1]), .K(1'b1), .Q(out_2[2]), .reset(and_1_out));  // open: Qn, preset
  and and_1 (and_1_out, out_2[2], out_2[1], j_k_ff_1_qn);

  assign out_2[3] = 1'b0;
endmodule

module C0_11 (
  input  in_1,
  output [3:0] out_2,
  output out_3
);

  wire and_1_out, j_k_ff_1_qn, j_k_ff_2_qn;

  J_K_Flip_Flop #(.trigger("falling")) j_k_ff_1 (
    .J(1'b1), .clk(in_1), .K(1'b1), .Q(out_2[0]), .Qn(j_k_ff_1_qn), .reset(and_1_out));  // open: preset
  J_K_Flip_Flop #(.trigger("falling")) j_k_ff_2 (
    .J(1'b1), .clk(out_2[0]), .K(1'b1), .Q(out_2[1]), .Qn(j_k_ff_2_qn), .reset(and_1_out));  // open: preset
  J_K_Flip_Flop #(.trigger("falling")) j_k_ff_3 (
    .J(1'b1), .clk(out_2[1]), .K(1'b1), .Q(out_2[2]), .reset(and_1_out));  // open: Qn, preset
  J_K_Flip_Flop #(.trigger("falling")) j_k_ff_4 (
    .J(1'b1), .clk(out_2[2]), .K(1'b1), .Q(out_2[3]), .reset(and_1_out));  // open: Qn, preset
  and and_1 (and_1_out, out_2[3], out_2[2], j_k_ff_2_qn, j_k_ff_1_qn);

  assign out_3 = out_2[3];
endmodule
