// Logisim project Decod letras.circ as structural Verilog
module Decod (
  input  [2:0] in_1,
  output a,
  output b,
  output c,
  output d,
  output e,
  output f,
  output g
);

  wire and_1_out, and_2_out, and_3_out, and_4_out, and_5_out, and_6_out, not_2_out, not_3_out, not_4_out,
       not_5_out, not_6_out, not_7_out, not_8_out, not_9_out, not_10_out, not_11_out;

  not not_1 (a, in_1[0]);
  not not_2 (not_2_out, in_1[1]);
  not not_3 (not_3_out, in_1[0]);
  not not_4 (not_4_out, in_1[1]);
  not not_5 (not_5_out, in_1[2]);
  not not_6 (not_6_out, in_1[1]);
  not not_7 (not_7_out, in_1[2]);
  not not_8 (not_8_out, in_1[0]);
  not not_9 (not_9_out, in_1[0]);
  not not_10 (not_10_out, in_1[1]);
  not not_11 (not_11_out, in_1[0]);
  and and_1 (and_1_out, not_2_out, in_1[0]);
  and and_2 (and_2_out, in_1[1], not_3_out);
  and and_3 (and_3_out, not_4_out, in_1[0]);
  and and_4 (and_4_out, not_5_out, not_6_out);
  or or_1 (e, not_7_out, not_8_out);
  or or_2 (f, not_9_out, in_1[1], in_1[2]);
  and and_5 (and_5_out, not_10_out, in_1[0]);
  and and_6 (and_6_out, in_1[1], not_11_out);
  or or_3 (b, and_1_out, and_2_out, in_1[2]);
  or or_4 (c, and_3_out, in_1[2]);
  or or_5 (d, and_4_out, in_1[0]);
  or or_6 (g, and_5_out, and_6_out, in_1[2]);
endmodule

module Teste (
  input  [2:0] in_1
);

  wire decod_1_a, decod_1_b, decod_1_c, decod_1_d, decod_1_e, decod_1_f, decod_1_g;

  Decod decod_1 (
    .a(decod_1_a), .b(decod_1_b), .c(decod_1_c), .d(decod_1_d), .e(decod_1_e), .f(decod_1_f), .g(decod_1_g),
    .in_1(in_1));
  _7_Segment_Display u_7_segment_display_1 (
    .g(decod_1_g), .f(decod_1_f), .a(decod_1_a), .b(decod_1_b), .e(decod_1_e), .d(decod_1_d), .c(decod_1_c));  // open: dp
endmodule
