// Logisim project SOMADOR DE 4BITS.circ as structural Verilog: 4 circuits, main circuit main
module main (
  input  [3:0] in_1,
  input  [3:0] in_2
);

  wire [3:0] somador4b_1_s;

  Somador4B somador4b_1 (.a(in_1), .s(somador4b_1_s), .b(in_2));
  Hex_Digit_Display hex_digit_display_1 (.value(somador4b_1_s));  // open: dp
endmodule

module MS (
  input  A,
  input  B,
  output S,
  output Ts
);

  xor xor_1 (S, A, B);
  and and_1 (Ts, A, B);
endmodule

module SC (
  input  A,
  input  B,
  input  Te,
  output S,
  output Ts
);

  wire and_1_out, and_2_out, and_3_out, xor_1_out;

  xor xor_1 (xor_1_out, A, B);
  and and_1 (and_1_out, A, B);
  and and_2 (and_2_out, A, Te);
  and and_3 (and_3_out, B, Te);
  xor xor_2 (S, xor_1_out, Te);
  or or_1 (Ts, and_1_out, and_2_out, and_3_out);
endmodule

// S4B
module Somador4B (
  input  [3:0] b,
  input  [3:0] a,
  output [3:0] s
);

  wire ms_1_ts, sc_2_ts, sc_3_ts;

  SC sc_1 (.S(s[3]), .A(a[3]), .B(b[3]), .Te(sc_3_ts));  // open: Ts
  SC sc_2 (.S(s[1]), .Ts(sc_2_ts), .A(a[1]), .B(b[1]), .Te(ms_1_ts));
  SC sc_3 (.S(s[2]), .Ts(sc_3_ts), .A(a[2]), .B(b[2]), .Te(sc_2_ts));
  MS ms_1 (.S(s[0]), .Ts(ms_1_ts), .A(a[0]), .B(b[0]));
endmodule
