// Logisim project SUBTRATOR 4BITS.circ as structural Verilog: 4 circuits, main circuit main
// Sub Comp
module main (
  input  [3:0] A,
  input  [3:0] B
);

  wire [3:0] sub4b_1_s;

  SUB4B sub4b_1 (.A(A), .B(B), .s(sub4b_1_s));
  Hex_Digit_Display hex_digit_display_1 (.value(sub4b_1_s));  // open: dp
endmodule

// Sub Comp
module SUB_COMP (
  input  A,
  input  B,
  input  TE,
  output S,
  output TS
);

  wire and_1_out, and_2_out, and_3_out, not_1_out, xor_1_out;

  not not_1 (not_1_out, A);
  xor xor_1 (xor_1_out, A, B);
  and and_1 (and_1_out, not_1_out, TE);
  and and_2 (and_2_out, not_1_out, B);
  and and_3 (and_3_out, B, TE);
  xor xor_2 (S, xor_1_out, TE);
  or or_1 (TS, and_1_out, and_2_out, and_3_out);
endmodule

// MSub
module MSUB (
  input  A,
  input  B,
  output S,
  output TS
);

  wire not_1_out;

  not not_1 (not_1_out, A);
  xor xor_1 (S, A, B);
  and and_1 (TS, not_1_out, B);
endmodule

module SUB4B (
  input  [3:0] A,
  input  [3:0] B,
  output [3:0] s
);

  wire msub_1_ts, sub_comp_2_ts, sub_comp_3_ts;

  SUB_COMP sub_comp_1 (.S(s[3]), .A(A[3]), .B(B[3]), .TE(sub_comp_2_ts));  // open: TS
  SUB_COMP sub_comp_2 (.S(s[2]), .TS(sub_comp_2_ts), .A(A[2]), .B(B[2]), .TE(sub_comp_3_ts));
  SUB_COMP sub_comp_3 (.S(s[1]), .TS(sub_comp_3_ts), .A(A[1]), .B(B[1]), .TE(msub_1_ts));
  MSUB msub_1 (.S(s[0]), .TS(msub_1_ts), .A(A[0]), .B(B[0]));
endmodule
