// Logisim project Somador e Subtrator.circ as structural Verilog: 4 circuits, main circuit main
module main (
  input  in_1
);

  wire _0_2_out, _0_out, _1_2_out, _1_out, _2_2_out, _2_out, _3_2_out, _3_out, _4_2_out, _4_out, _5_2_out,
       _5_out, _6_2_out, _6_out, _7_2_out, _7_out, _8_2_out, _8_out, _9_2_out, _9_out, decod7s_1_p2,
       decod7s_1_p3, decod7s_1_p4, decod7s_1_p5, decod7s_1_p6, decod7s_1_p7, decod7s_1_p8;
  wire [3:0] ss4b_1_out_4, teclado_1_out_11, teclado_2_out_11;

  Button _1 (.out(_1_out));
  Button _0 (.out(_0_out));
  Teclado teclado_1 (
    .out_11(teclado_1_out_11), .in_1(_0_out), .in_2(_1_out), .in_3(_2_out), .in_4(_3_out), .in_5(_4_out),
    .in_6(_5_out), .in_7(_6_out), .in_8(_7_out), .in_9(_8_out), .in_10(_9_out));
  Button _2 (.out(_2_out));
  Button _4 (.out(_4_out));
  Button _5 (.out(_5_out));
  Button _3 (.out(_3_out));
  Button _9 (.out(_9_out));
  Button _7 (.out(_7_out));
  Button _6 (.out(_6_out));
  Button _8 (.out(_8_out));
  Hex_Digit_Display hex_digit_display_1 (.value(teclado_1_out_11));  // open: dp
  Button _1_2 (.out(_1_2_out));
  Button _0_2 (.out(_0_2_out));
  Teclado teclado_2 (
    .out_11(teclado_2_out_11), .in_1(_0_2_out), .in_2(_1_2_out), .in_3(_2_2_out), .in_4(_3_2_out),
    .in_5(_4_2_out), .in_6(_5_2_out), .in_7(_6_2_out), .in_8(_7_2_out), .in_9(_8_2_out), .in_10(_9_2_out));
  SS4B ss4b_1 (.a(teclado_1_out_11), .in_3(in_1), .b(teclado_2_out_11), .out_4(ss4b_1_out_4));
  Button _3_2 (.out(_3_2_out));
  Button _2_2 (.out(_2_2_out));
  Button _5_2 (.out(_5_2_out));
  Button _4_2 (.out(_4_2_out));
  Hex_Digit_Display hex_digit_display_2 (.value(teclado_2_out_11));  // open: dp
  Button _8_2 (.out(_8_2_out));
  Button _6_2 (.out(_6_2_out));
  Button _7_2 (.out(_7_2_out));
  Button _9_2 (.out(_9_2_out));
  // Decod7s decod7s_1: pin names not known; wires that end beside it: ss4b_1_out_4, decod7s_1_p2, decod7s_1_p3, decod7s_1_p4, decod7s_1_p5, decod7s_1_p6, decod7s_1_p7, decod7s_1_p8
  _7_Segment_Display u_7_segment_display_1 (
    .g(decod7s_1_p8), .f(decod7s_1_p7), .a(decod7s_1_p2), .b(decod7s_1_p3), .e(decod7s_1_p6),
    .d(decod7s_1_p5), .c(decod7s_1_p4));  // open: dp
endmodule

module SSC (
  input  O,
  input  A,
  input  B,
  input  Te,
  output S,
  output Ts
);

  wire and_1_out, and_2_out, or_1_out, xor_1_out, xor_2_out;

  xor xor_1 (xor_1_out, A, B);
  and and_1 (and_1_out, B, Te);
  xor xor_2 (xor_2_out, O, A);
  or or_1 (or_1_out, Te, B);
  xor xor_3 (S, xor_1_out, Te);
  and and_2 (and_2_out, xor_2_out, or_1_out);
  or or_2 (Ts, and_1_out, and_2_out);
endmodule

module SS4B (
  input  [3:0] a,
  input  [3:0] b,
  input  in_3,
  output [3:0] out_4
);

  wire mss_1_ts, ssc_2_ts, ssc_3_ts;

  SSC ssc_1 (.S(out_4[3]), .O(in_3), .A(a[3]), .B(b[3]), .Te(ssc_2_ts));  // open: Ts
  SSC ssc_2 (.S(out_4[2]), .Ts(ssc_2_ts), .O(in_3), .A(a[2]), .B(b[2]), .Te(ssc_3_ts));
  SSC ssc_3 (.S(out_4[1]), .Ts(ssc_3_ts), .O(in_3), .A(a[1]), .B(b[1]), .Te(mss_1_ts));
  MSS mss_1 (.O(in_3), .A(a[0]), .B(b[0]), .Ts(mss_1_ts), .S(out_4[0]));
endmodule

// MMS
module MSS (
  input  O,
  input  A,
  input  B,
  output S,
  output Ts
);

  wire xor_2_out;

  xor xor_1 (S, A, B);
  xor xor_2 (xor_2_out, O, A);
  and and_1 (Ts, xor_2_out, B);
endmodule
